// Logisim project project.circ as structural Verilog: 3 circuits, main circuit main
// rising
module main (
);

  wire and_1_out, and_2_out, and_3_out, and_4_out, and_5_out, and_6_out, and_7_out, button_1_out,
       button_2_out, button_3_out, button_4_out, cdm_16_1_p1, cdm_16_1_p3, cdm_16_1_p4, cdm_16_1_p5,
       cdm_16_1_p7, cdm_16_1_p8, cdm_16_1_p9, cdm_16_1_p10, cdm_16_1_p11, cdm_16_1_p12, clk, comparator_1_eq,
       comparator_2_eq, comparator_3_eq, comparator_4_eq, demultiplexer_1_out0, demultiplexer_1_out1,
       demultiplexer_1_out2, demultiplexer_2_out0, demultiplexer_2_out1, demultiplexer_2_out2,
       demultiplexer_2_out3, demultiplexer_2_out4, demultiplexer_2_out5, demultiplexer_2_out6,
       demultiplexer_2_out7, demultiplexer_2_out8, demultiplexer_2_out9, demultiplexer_2_out10,
       demultiplexer_2_out11, demultiplexer_2_out12, demultiplexer_2_out13, demultiplexer_2_out14,
       demultiplexer_2_out15, demultiplexer_2_out16, demultiplexer_2_out17, demultiplexer_2_out18,
       demultiplexer_2_out19, demultiplexer_2_out20, demultiplexer_2_out21, demultiplexer_2_out22,
       demultiplexer_2_out23, demultiplexer_2_out24, demultiplexer_2_out25, demultiplexer_2_out26,
       demultiplexer_2_out27, demultiplexer_2_out28, demultiplexer_2_out29, demultiplexer_2_out30,
       demultiplexer_2_out31, jIAck, jIRQ, not_1_out, or_1_out, priority_encoder_1_gs;
  wire [1:0] joystick_1_x, joystick_1_y, priority_encoder_1_out;
  wire [5:0] cdm_16_1_p2;
  wire [7:0] ram_1_p6, ram_1_p6_2, selector_q, undriven;
  wire [15:0] cdm_16_1_p13, cdm_16_1_p14, cdm_16_1_p15, joy;
  wire [31:0] lo_q, register_1_q, register_2_q, register_3_q, register_4_q, register_5_q, register_6_q,
       register_7_q, register_8_q, register_9_q, register_10_q, register_11_q, register_12_q, register_13_q,
       register_14_q, register_15_q, register_16_q, register_17_q, register_18_q, register_19_q,
       register_20_q, register_21_q, register_22_q, register_23_q, register_24_q, register_25_q,
       register_26_q, register_27_q, register_28_q, register_29_q, register_30_q, register_31_q,
       register_32_q;

  // Probe on cdm_16_1_p5
  // Probe on cdm_16_1_p4
  // CdM_16 cdm_16_1: pin names not known; wires that end beside it: cdm_16_1_p1, cdm_16_1_p2, cdm_16_1_p3, cdm_16_1_p4, cdm_16_1_p5, clk, cdm_16_1_p7, cdm_16_1_p8, cdm_16_1_p9, cdm_16_1_p10, cdm_16_1_p11, cdm_16_1_p12, cdm_16_1_p13, cdm_16_1_p14, cdm_16_1_p15
  interrupt_arbiter interrupt_arbiter_1 (
    .IRQ_out(cdm_16_1_p1), .vec_out(cdm_16_1_p2), .IAck_out(cdm_16_1_p3), .IRQ_1(jIRQ), .vec_1(6'b000101),
    .IAck_1(jIAck), .clk(clk));  // open: IRQ_2, vec_2, IAck_2
  // Probe on cdm_16_1_p7
  // Probe on cdm_16_1_p9
  // Probe on cdm_16_1_p8
  Comparator #(.width(16), .mode("unsigned")) comparator_1 (
    .a(16'h82), .b(cdm_16_1_p13), .eq(comparator_1_eq));  // open: gt, lt
  Comparator #(.width(16), .mode("unsigned")) comparator_2 (
    .a(16'h80), .b(cdm_16_1_p13), .eq(comparator_2_eq));  // open: gt, lt
  Comparator #(.width(16), .mode("unsigned")) comparator_3 (
    .a(16'h84), .b(cdm_16_1_p13), .eq(comparator_3_eq));  // open: gt, lt
  Comparator #(.width(16), .mode("unsigned")) comparator_4 (
    .a(16'h85), .b(cdm_16_1_p13), .eq(comparator_4_eq));  // open: gt, lt
  and and_1 (and_1_out, ~priority_encoder_1_gs, cdm_16_1_p10);  // AND_Gate
  and and_2 (and_2_out, comparator_1_eq, cdm_16_1_p10);
  and and_3 (and_3_out, comparator_2_eq, cdm_16_1_p10);
  and and_4 (and_4_out, comparator_3_eq, cdm_16_1_p10);
  and and_5 (and_5_out, comparator_4_eq, cdm_16_1_p10);
  // RAM ram_1: pin names not known; wires that end beside it: cdm_16_1_p13, cdm_16_1_p12, and_1_out, clk, cdm_16_1_p11, {ram_1_p6_2, ram_1_p6}
  not not_1 (not_1_out, cdm_16_1_p11);
  assign {ram_1_p6_2, ram_1_p6} = not_1_out ? cdm_16_1_p14 : 16'bz;  // Controlled_Buffer controlled_buffer_1
  assign cdm_16_1_p15 = cdm_16_1_p11 ? {ram_1_p6_2, ram_1_p6} : 16'bz;  // Controlled_Buffer controlled_buffer_2
  Priority_Encoder #(.select(2)) priority_encoder_1 (
    .in0(and_2_out), .in1(and_3_out), .in2(and_4_out), .in3(and_5_out), .out(priority_encoder_1_out),
    .gs(priority_encoder_1_gs));  // open: en_out, en_in
  Multiplexer #(.select(2), .width(16)) multiplexer_1 (
    .in0(lo_q[15:0]), .in1(lo_q[31:16]), .in2({undriven, selector_q}), .in3(joy),
    .out({ram_1_p6_2, ram_1_p6}), .sel(priority_encoder_1_out), .en(and_6_out));
  and and_6 (and_6_out, priority_encoder_1_gs, cdm_16_1_p10, cdm_16_1_p11);
  Demultiplexer #(.select(2), .disabled(0)) demultiplexer_1 (
    .out0(demultiplexer_1_out0), .out1(demultiplexer_1_out1), .out2(demultiplexer_1_out2), .in(1'b1),
    .sel(priority_encoder_1_out), .en(and_7_out));  // open: out3
  and and_7 (and_7_out, priority_encoder_1_gs, cdm_16_1_p10, ~cdm_16_1_p11);  // AND_Gate
  Clock clock_1 (.out(clk));
  Register #(.width(16)) lo (
    .D({ram_1_p6_2, ram_1_p6}), .en(demultiplexer_1_out0), .Q(lo_q[15:0]), .clk(clk));  // open: clr
  Register #(.width(16)) lo_2 (
    .D({ram_1_p6_2, ram_1_p6}), .en(demultiplexer_1_out1), .Q(lo_q[31:16]), .clk(clk));  // open: clr
  Register selector (.D(ram_1_p6), .en(demultiplexer_1_out2), .Q(selector_q), .clk(clk));  // open: clr
  or or_1 (or_1_out, demultiplexer_1_out1, demultiplexer_1_out0);
  Demultiplexer #(.select(5), .disabled(0)) demultiplexer_2 (
    .out0(demultiplexer_2_out0), .out1(demultiplexer_2_out1), .out2(demultiplexer_2_out2),
    .out3(demultiplexer_2_out3), .out4(demultiplexer_2_out4), .out5(demultiplexer_2_out5),
    .out6(demultiplexer_2_out6), .out7(demultiplexer_2_out7), .out8(demultiplexer_2_out8),
    .out9(demultiplexer_2_out9), .out10(demultiplexer_2_out10), .out11(demultiplexer_2_out11),
    .out12(demultiplexer_2_out12), .out13(demultiplexer_2_out13), .out14(demultiplexer_2_out14),
    .out15(demultiplexer_2_out15), .out16(demultiplexer_2_out16), .out17(demultiplexer_2_out17),
    .out18(demultiplexer_2_out18), .out19(demultiplexer_2_out19), .out20(demultiplexer_2_out20),
    .out21(demultiplexer_2_out21), .out22(demultiplexer_2_out22), .out23(demultiplexer_2_out23),
    .out24(demultiplexer_2_out24), .out25(demultiplexer_2_out25), .out26(demultiplexer_2_out26),
    .out27(demultiplexer_2_out27), .out28(demultiplexer_2_out28), .out29(demultiplexer_2_out29),
    .out30(demultiplexer_2_out30), .out31(demultiplexer_2_out31), .in(1'b1), .sel(selector_q[4:0]),
    .en(or_1_out));
  Register #(.width(32), .trigger("falling")) register_1 (
    .D(lo_q), .en(demultiplexer_2_out0), .Q(register_1_q), .clk(clk));  // open: clr
  Register #(.width(32), .trigger("falling")) register_2 (
    .D(lo_q), .en(demultiplexer_2_out1), .Q(register_2_q), .clk(clk));  // open: clr
  Register #(.width(32), .trigger("falling")) register_3 (
    .D(lo_q), .en(demultiplexer_2_out2), .Q(register_3_q), .clk(clk));  // open: clr
  Register #(.width(32), .trigger("falling")) register_4 (
    .D(lo_q), .en(demultiplexer_2_out3), .Q(register_4_q), .clk(clk));  // open: clr
  Register #(.width(32), .trigger("falling")) register_5 (
    .D(lo_q), .en(demultiplexer_2_out4), .Q(register_5_q), .clk(clk));  // open: clr
  Register #(.width(32), .trigger("falling")) register_6 (
    .D(lo_q), .en(demultiplexer_2_out5), .Q(register_6_q), .clk(clk));  // open: clr
  Register #(.width(32), .trigger("falling")) register_7 (
    .D(lo_q), .en(demultiplexer_2_out6), .Q(register_7_q), .clk(clk));  // open: clr
  Register #(.width(32), .trigger("falling")) register_8 (
    .D(lo_q), .en(demultiplexer_2_out7), .Q(register_8_q), .clk(clk));  // open: clr
  Register #(.width(32), .trigger("falling")) register_9 (
    .D(lo_q), .en(demultiplexer_2_out8), .Q(register_9_q), .clk(clk));  // open: clr
  Register #(.width(32), .trigger("falling")) register_10 (
    .D(lo_q), .en(demultiplexer_2_out9), .Q(register_10_q), .clk(clk));  // open: clr
  Register #(.width(32), .trigger("falling")) register_11 (
    .D(lo_q), .en(demultiplexer_2_out10), .Q(register_11_q), .clk(clk));  // open: clr
  Register #(.width(32), .trigger("falling")) register_12 (
    .D(lo_q), .en(demultiplexer_2_out11), .Q(register_12_q), .clk(clk));  // open: clr
  Register #(.width(32), .trigger("falling")) register_13 (
    .D(lo_q), .en(demultiplexer_2_out12), .Q(register_13_q), .clk(clk));  // open: clr
  Register #(.width(32), .trigger("falling")) register_14 (
    .D(lo_q), .en(demultiplexer_2_out13), .Q(register_14_q), .clk(clk));  // open: clr
  Register #(.width(32), .trigger("falling")) register_15 (
    .D(lo_q), .en(demultiplexer_2_out14), .Q(register_15_q), .clk(clk));  // open: clr
  Register #(.width(32), .trigger("falling")) register_16 (
    .D(lo_q), .en(demultiplexer_2_out15), .Q(register_16_q), .clk(clk));  // open: clr
  Register #(.width(32), .trigger("falling")) register_17 (
    .D(lo_q), .en(demultiplexer_2_out16), .Q(register_17_q), .clk(clk));  // open: clr
  Register #(.width(32), .trigger("falling")) register_18 (
    .D(lo_q), .en(demultiplexer_2_out17), .Q(register_18_q), .clk(clk));  // open: clr
  Register #(.width(32), .trigger("falling")) register_19 (
    .D(lo_q), .en(demultiplexer_2_out18), .Q(register_19_q), .clk(clk));  // open: clr
  Register #(.width(32), .trigger("falling")) register_20 (
    .D(lo_q), .en(demultiplexer_2_out19), .Q(register_20_q), .clk(clk));  // open: clr
  Register #(.width(32), .trigger("falling")) register_21 (
    .D(lo_q), .en(demultiplexer_2_out20), .Q(register_21_q), .clk(clk));  // open: clr
  Register #(.width(32), .trigger("falling")) register_22 (
    .D(lo_q), .en(demultiplexer_2_out21), .Q(register_22_q), .clk(clk));  // open: clr
  Register #(.width(32), .trigger("falling")) register_23 (
    .D(lo_q), .en(demultiplexer_2_out22), .Q(register_23_q), .clk(clk));  // open: clr
  Register #(.width(32), .trigger("falling")) register_24 (
    .D(lo_q), .en(demultiplexer_2_out23), .Q(register_24_q), .clk(clk));  // open: clr
  Register #(.width(32), .trigger("falling")) register_25 (
    .D(lo_q), .en(demultiplexer_2_out24), .Q(register_25_q), .clk(clk));  // open: clr
  Register #(.width(32), .trigger("falling")) register_26 (
    .D(lo_q), .en(demultiplexer_2_out25), .Q(register_26_q), .clk(clk));  // open: clr
  Register #(.width(32), .trigger("falling")) register_27 (
    .D(lo_q), .en(demultiplexer_2_out26), .Q(register_27_q), .clk(clk));  // open: clr
  Register #(.width(32), .trigger("falling")) register_28 (
    .D(lo_q), .en(demultiplexer_2_out27), .Q(register_28_q), .clk(clk));  // open: clr
  Register #(.width(32), .trigger("falling")) register_29 (
    .D(lo_q), .en(demultiplexer_2_out28), .Q(register_29_q), .clk(clk));  // open: clr
  Register #(.width(32), .trigger("falling")) register_30 (
    .D(lo_q), .en(demultiplexer_2_out29), .Q(register_30_q), .clk(clk));  // open: clr
  Register #(.width(32), .trigger("falling")) register_31 (
    .D(lo_q), .en(demultiplexer_2_out30), .Q(register_31_q), .clk(clk));  // open: clr
  Register #(.width(32), .trigger("falling")) register_32 (
    .D(lo_q), .en(demultiplexer_2_out31), .Q(register_32_q), .clk(clk));  // open: clr
  DotMatrix #(.inputtype("row"), .matrixcols(32), .matrixrows(32)) dotmatrix_1 (
    .row0(register_1_q), .row1(register_2_q), .row2(register_3_q), .row3(register_4_q), .row4(register_5_q),
    .row5(register_6_q), .row6(register_7_q), .row7(register_8_q), .row8(register_9_q), .row9(register_10_q),
    .row10(register_11_q), .row11(register_12_q), .row12(register_13_q), .row13(register_14_q),
    .row14(register_15_q), .row15(register_16_q), .row16(register_17_q), .row17(register_18_q),
    .row18(register_19_q), .row19(register_20_q), .row20(register_21_q), .row21(register_22_q),
    .row22(register_23_q), .row23(register_24_q), .row24(register_25_q), .row25(register_26_q),
    .row26(register_27_q), .row27(register_28_q), .row28(register_29_q), .row29(register_30_q),
    .row30(register_31_q), .row31(register_32_q));
  Button button_1 (.out(button_1_out));
  Joystick #(.bits(2)) joystick_1 (.x(joystick_1_x), .y(joystick_1_y));
  gamepad gamepad_1 (
    .data(joy), .joy({joystick_1_y, joystick_1_x}), .B(button_3_out), .A(button_4_out), .R(button_2_out),
    .IAck(jIAck), .clk(clk), .IRQ(jIRQ), .L(button_1_out));
  Button button_2 (.out(button_2_out));
  Button button_3 (.out(button_3_out));
  Button button_4 (.out(button_4_out));
endmodule

module interrupt_arbiter (
  input  IRQ_2,
  input  [5:0] vec_2,
  input  IAck_out,
  input  IRQ_1,
  input  [5:0] vec_1,
  input  clk,
  output IRQ_out,
  output [5:0] vec_out,
  output IAck_2,
  output IAck_1
);

  wire and_2_out, and_3_out, and_4_out, and_5_out, and_7_out, and_8_out, d_ff_1_q, d_ff_2_q, or_1_out,
       or_2_out;

  and and_1 (IAck_2, d_ff_1_q, IAck_out);
  and and_2 (and_2_out, IRQ_2, ~IRQ_1, ~d_ff_2_q);  // AND_Gate
  and and_3 (and_3_out, d_ff_1_q, IAck_out);
  and and_4 (and_4_out, ~d_ff_1_q, IRQ_1);  // AND_Gate
  and and_5 (and_5_out, d_ff_2_q, IAck_out);
  and and_6 (IAck_1, IAck_out, d_ff_2_q);
  or or_1 (or_1_out, and_2_out, and_3_out);
  or or_2 (or_2_out, and_4_out, and_5_out);
  D_Flip_Flop d_ff_1 (.clk(clk), .D(or_1_out), .Q(d_ff_1_q));  // open: Qn, preset, en, reset
  D_Flip_Flop d_ff_2 (.clk(clk), .D(or_2_out), .Q(d_ff_2_q));  // open: Qn, preset, en, reset
  and and_7 (and_7_out, d_ff_1_q, IAck_out);
  assign vec_out = and_7_out ? vec_2 : 6'bz;  // Controlled_Buffer controlled_buffer_1
  and and_8 (and_8_out, d_ff_2_q, IAck_out);
  assign vec_out = and_8_out ? vec_1 : 6'bz;  // Controlled_Buffer controlled_buffer_2
  assign IRQ_out = d_ff_1_q ? IRQ_2 : 1'bz;  // Controlled_Buffer controlled_buffer_3
  Pull_Resistor pull_resistor_1 (.node(IRQ_out));
  assign IRQ_out = d_ff_2_q ? IRQ_1 : 1'bz;  // Controlled_Buffer controlled_buffer_4
endmodule

module gamepad (
  input  IAck,
  input  clk,
  input  [3:0] joy,
  input  R,
  input  L,
  input  B,
  input  A,
  output [15:0] data,
  output IRQ
);

  wire and_5_out, comparator_1_eq;
  wire [5:2] and_3_out;
  wire [15:0] register_1_q;

  and and_1 (and_3_out[4], joy[0], joy[1]);
  and and_2 (and_3_out[5], joy[0], ~joy[1]);  // AND_Gate
  and and_3 (and_3_out[2], joy[2], joy[3]);
  and and_4 (and_3_out[3], joy[2], ~joy[3]);  // AND_Gate
  Register #(.width(16)) register_1 (
    .D({{8{1'b0}}, L, R, and_3_out, B, A}), .en(and_5_out), .Q(register_1_q), .clk(clk));  // open: clr
  and and_5 (and_5_out, ~IAck, comparator_1_eq);  // AND_Gate
  Register #(.width(16), .trigger("falling")) register_2 (
    .D(register_1_q), .en(IAck), .Q(data), .clk(clk));  // open: clr
  Comparator #(.width(16), .mode("unsigned")) comparator_1 (
    .a(data), .b(register_1_q), .eq(comparator_1_eq));  // open: gt, lt
  not not_1 (IRQ, comparator_1_eq);
endmodule
